# Fritzing sketch Fritzing_sketch (saved by Fritzing 0.9.3b)
breadboards: 1

parts:
  U1 = NodeMCU V1.0
  DHT1 = DHT22 Humidity and Temperature Sensor

nets:
  N1: U1.D4, DHT1.DATA
  3V3: U1.3V3, DHT1.VDD
  GND: U1.GND, DHT1.GND

custom parts:
  NodeMCU V1.0: ESP8266 based NodeMCU
